// Logisim project P3cpu.circ as structural Verilog: 9 circuits, main circuit main
module main (
  input  in_1,
  output [4:0] A3,
  output [31:0] out_3,
  output [31:0] out_4,
  output [31:0] out_5,
  output out_6,
  output out_7,
  output [31:0] out_8,
  output [31:0] out_9
);

  wire ALUsrc, clk, EXTOp, isnew, zero;
  wire [1:0] MemtoReg, RegDst;
  wire [2:0] NPCslt;
  wire [3:0] \type ;
  wire [4:0] undriven;
  wire [15:0] imm16;
  wire [25:0] imm26;
  wire [31:0] dm_1_data, ext_1_out_3, grf_1_rd1, multiplexer_3_out, npc_1_npc, PC_4, ra, undriven_2;

  Clock clock_1 (.out(clk));
  NPC npc_1 (.PC(out_5), .imm16(imm16), .NPC(npc_1_npc), .imm26(imm26), .NPCslt(NPCslt), .GRF(ra), .zero(zero));
  Adder #(.width(32)) adder_1 (.a(out_5), .b(32'h4), .out(PC_4));  // open: cin, cout
  PC pc_1 (.NPC(npc_1_npc), .PC(out_5), .reset(in_1), .clk(clk));
  Comparator #(.width(4), .mode("unsigned")) comparator_1 (.a(\type ), .b(4'b1011), .eq(isnew));  // open: gt, lt
  IM im_1 (.PC(out_5), .opcode(out_3));
  Controler controler_1 (
    .NPCslt(NPCslt), .grfWE(out_6), .\type (\type ), .EXTOp(EXTOp), .ALUsrc(ALUsrc), .RegDst(RegDst),
    .MomtoReg(MemtoReg), .DMWE(out_7), .in_1(out_3[31:26]), .in_2(out_3[5:0]));
  Bit_Extender #(.in_width(32)) bit_extender_1 (.in(out_3), .out(imm16));
  Bit_Extender #(.in_width(32), .out_width(26)) bit_extender_2 (.in(out_3), .out(imm26));
  Multiplexer #(.select(2), .width(5)) multiplexer_1 (
    .in0(out_3[20:16]), .in1(out_3[15:11]), .in2({5{1'b1}}), .in3(undriven), .out(A3), .sel(RegDst));  // open: en
  Multiplexer #(.select(2), .width(32)) multiplexer_2 (
    .in0(out_8), .in1(dm_1_data), .in2(PC_4), .in3(undriven_2), .out(out_4), .sel(MemtoReg));  // open: en
  grf grf_1 (
    .WE(out_6), .A3(A3), .CLK(clk), .WD(out_4), .Reset(in_1), .A1(out_3[25:21]), .RD1(grf_1_rd1),
    .A2(out_3[20:16]), .RD2(out_9));
  EXT ext_1 (.in_1(imm16), .EXTOp(EXTOp), .out_3(ext_1_out_3));
  Multiplexer #(.width(32)) multiplexer_3 (
    .in0(out_9), .in1(ext_1_out_3), .out(multiplexer_3_out), .sel(ALUsrc));  // open: en
  ALU alu_1 (.out_4(out_8), .zero(zero), .\type (\type ), .inA(grf_1_rd1), .inB(multiplexer_3_out));
  DM dm_1 (.Addr(out_8), .WD(out_9), .Data(dm_1_data), .WE(out_7), .clk(clk), .Re(in_1));  // open: byte

  // Other names for the same wires on the sheet: DMWE = out_7; grfWE = out_6; func[5:0] = out_3[5:0];
  //   Instr[31:0] = out_3; opcode[5:0] = out_3[31:26]; PC[31:0] = out_5; Re = in_1; WD[31:0] = out_9

  // Notes on the sheet:
  //   PC
  //   1011
  //   IM
  //   Control
  //   grfWD
  //   grf
  //   ALU
  //   Addr
  //   DMWD
endmodule

module NPC (
  input  [31:0] PC,
  input  zero,
  input  [15:0] imm16,
  input  [31:0] GRF,
  input  [25:0] imm26,
  input  [2:0] NPCslt,
  output [31:0] NPC
);

  wire [31:0] adder_1_out, adder_2_out, bit_extender_1_out, multiplexer_1_out;

  Adder #(.width(32)) adder_1 (.a(32'h4), .b(PC), .out(adder_1_out));  // open: cin, cout
  assign bit_extender_1_out = {{14{imm16[15]}}, {imm16, 2'b00}};  // Bit_Extender bit_extender_1
  Adder #(.width(32)) adder_2 (.a(adder_1_out), .b(bit_extender_1_out), .out(adder_2_out));  // open: cin, cout
  Multiplexer #(.width(32)) multiplexer_1 (
    .in0(adder_1_out), .in1(adder_2_out), .out(multiplexer_1_out), .sel(zero));  // open: en
  Multiplexer #(.select(3), .width(32), .disabled(0)) multiplexer_2 (
    .in0(adder_1_out), .in1(multiplexer_1_out), .in2({PC[31:28], imm26, 2'b00}), .in3(GRF), .out(NPC),
    .sel(NPCslt));  // open: in4, in5, in6, in7, en
endmodule

module grf (
  input  WE,
  input  [4:0] A3,
  input  CLK,
  input  [4:0] A1,
  input  [4:0] A2,
  input  Reset,
  input  [31:0] WD,
  output [31:0] RD2,
  output [31:0] RD1
);

  wire and_1_out, and_2_out, and_3_out, and_4_out, and_5_out, and_6_out, and_7_out, and_8_out, and_9_out,
       and_10_out, and_11_out, and_12_out, and_13_out, and_14_out, and_15_out, and_16_out, and_17_out,
       and_18_out, and_19_out, and_20_out, and_21_out, and_22_out, and_23_out, and_24_out, and_25_out,
       and_26_out, and_27_out, and_28_out, and_29_out, and_30_out, and_31_out, and_32_out, decoder_1_out0,
       decoder_1_out1, decoder_1_out2, decoder_1_out3, decoder_1_out4, decoder_1_out5, decoder_1_out6,
       decoder_1_out7, decoder_1_out8, decoder_1_out9, decoder_1_out10, decoder_1_out11, decoder_1_out12,
       decoder_1_out13, decoder_1_out14, decoder_1_out15, decoder_1_out16, decoder_1_out17, decoder_1_out18,
       decoder_1_out19, decoder_1_out20, decoder_1_out21, decoder_1_out22, decoder_1_out23, decoder_1_out24,
       decoder_1_out25, decoder_1_out26, decoder_1_out27, decoder_1_out28, decoder_1_out29, decoder_1_out30,
       decoder_1_out31;
  wire [31:0] _0, _1, _2, _3, _4, _5, _6, _7, _8, _9, _10, _11, _12, _13, _14, _15, _16, _17, _18, _19, _20,
       _21, _22, _23, _24, _25, _26, _27, _28, _29, _30, _31, register_1_q, register_2_q, register_3_q,
       register_4_q, register_5_q, register_6_q, register_7_q, register_8_q, register_9_q, register_10_q,
       register_11_q, register_12_q, register_13_q, register_14_q, register_15_q, register_16_q,
       register_17_q, register_18_q, register_19_q, register_20_q, register_21_q, register_22_q,
       register_23_q, register_24_q, register_25_q, register_26_q, register_27_q, register_28_q,
       register_29_q, register_30_q, register_31_q, register_32_q;

  Decoder #(.select(5)) decoder_1 (
    .out0(decoder_1_out0), .out1(decoder_1_out1), .out2(decoder_1_out2), .out3(decoder_1_out3),
    .out4(decoder_1_out4), .out5(decoder_1_out5), .out6(decoder_1_out6), .out7(decoder_1_out7),
    .out8(decoder_1_out8), .out9(decoder_1_out9), .out10(decoder_1_out10), .out11(decoder_1_out11),
    .out12(decoder_1_out12), .out13(decoder_1_out13), .out14(decoder_1_out14), .out15(decoder_1_out15),
    .out16(decoder_1_out16), .out17(decoder_1_out17), .out18(decoder_1_out18), .out19(decoder_1_out19),
    .out20(decoder_1_out20), .out21(decoder_1_out21), .out22(decoder_1_out22), .out23(decoder_1_out23),
    .out24(decoder_1_out24), .out25(decoder_1_out25), .out26(decoder_1_out26), .out27(decoder_1_out27),
    .out28(decoder_1_out28), .out29(decoder_1_out29), .out30(decoder_1_out30), .out31(decoder_1_out31),
    .sel(A3));  // open: en
  Demultiplexer #(.select(5), .width(32), .tristate("true")) demultiplexer_1 (
    .out0(_0), .out1(_1), .out2(_2), .out3(_3), .out4(_4), .out5(_5), .out6(_6), .out7(_7), .out8(_8),
    .out9(_9), .out10(_10), .out11(_11), .out12(_12), .out13(_13), .out14(_14), .out15(_15), .out16(_16),
    .out17(_17), .out18(_18), .out19(_19), .out20(_20), .out21(_21), .out22(_22), .out23(_23), .out24(_24),
    .out25(_25), .out26(_26), .out27(_27), .out28(_28), .out29(_29), .out30(_30), .out31(_31), .in(WD),
    .sel(A3));  // open: en
  and and_1 (and_1_out, WE, decoder_1_out0);
  and and_2 (and_2_out, WE, decoder_1_out1);
  and and_3 (and_3_out, WE, decoder_1_out2);
  and and_4 (and_4_out, WE, decoder_1_out3);
  and and_5 (and_5_out, WE, decoder_1_out4);
  and and_6 (and_6_out, WE, decoder_1_out5);
  and and_7 (and_7_out, WE, decoder_1_out6);
  and and_8 (and_8_out, WE, decoder_1_out7);
  and and_9 (and_9_out, WE, decoder_1_out8);
  and and_10 (and_10_out, WE, decoder_1_out9);
  and and_11 (and_11_out, WE, decoder_1_out10);
  and and_12 (and_12_out, WE, decoder_1_out11);
  and and_13 (and_13_out, WE, decoder_1_out12);
  and and_14 (and_14_out, WE, decoder_1_out13);
  and and_15 (and_15_out, WE, decoder_1_out14);
  and and_16 (and_16_out, WE, decoder_1_out15);
  and and_17 (and_17_out, WE, decoder_1_out16);
  and and_18 (and_18_out, WE, decoder_1_out17);
  and and_19 (and_19_out, WE, decoder_1_out18);
  and and_20 (and_20_out, WE, decoder_1_out19);
  and and_21 (and_21_out, WE, decoder_1_out20);
  and and_22 (and_22_out, WE, decoder_1_out21);
  and and_23 (and_23_out, WE, decoder_1_out22);
  and and_24 (and_24_out, WE, decoder_1_out23);
  and and_25 (and_25_out, WE, decoder_1_out24);
  and and_26 (and_26_out, WE, decoder_1_out25);
  and and_27 (and_27_out, WE, decoder_1_out26);
  and and_28 (and_28_out, WE, decoder_1_out27);
  and and_29 (and_29_out, WE, decoder_1_out28);
  and and_30 (and_30_out, WE, decoder_1_out29);
  and and_31 (and_31_out, WE, decoder_1_out30);
  and and_32 (and_32_out, WE, decoder_1_out31);
  Register #(.width(32)) register_1 (.D(_0), .en(and_1_out), .Q(register_1_q), .clk(CLK), .clr(1'b1));
  Register #(.width(32)) register_2 (.D(_1), .en(and_2_out), .Q(register_2_q), .clk(CLK), .clr(Reset));
  Register #(.width(32)) register_3 (.D(_2), .en(and_3_out), .Q(register_3_q), .clk(CLK), .clr(Reset));
  Register #(.width(32)) register_4 (.D(_3), .en(and_4_out), .Q(register_4_q), .clk(CLK), .clr(Reset));
  Register #(.width(32)) register_5 (.D(_4), .en(and_5_out), .Q(register_5_q), .clk(CLK), .clr(Reset));
  Register #(.width(32)) register_6 (.D(_5), .en(and_6_out), .Q(register_6_q), .clk(CLK), .clr(Reset));
  Register #(.width(32)) register_7 (.D(_6), .en(and_7_out), .Q(register_7_q), .clk(CLK), .clr(Reset));
  Register #(.width(32)) register_8 (.D(_7), .en(and_8_out), .Q(register_8_q), .clk(CLK), .clr(Reset));
  Register #(.width(32)) register_9 (.D(_8), .en(and_9_out), .Q(register_9_q), .clk(CLK), .clr(Reset));
  Register #(.width(32)) register_10 (.D(_9), .en(and_10_out), .Q(register_10_q), .clk(CLK), .clr(Reset));
  Register #(.width(32)) register_11 (.D(_10), .en(and_11_out), .Q(register_11_q), .clk(CLK), .clr(Reset));
  Register #(.width(32)) register_12 (.D(_11), .en(and_12_out), .Q(register_12_q), .clk(CLK), .clr(Reset));
  Register #(.width(32)) register_13 (.D(_12), .en(and_13_out), .Q(register_13_q), .clk(CLK), .clr(Reset));
  Register #(.width(32)) register_14 (.D(_13), .en(and_14_out), .Q(register_14_q), .clk(CLK), .clr(Reset));
  Register #(.width(32)) register_15 (.D(_14), .en(and_15_out), .Q(register_15_q), .clk(CLK), .clr(Reset));
  Register #(.width(32)) register_16 (.D(_15), .en(and_16_out), .Q(register_16_q), .clk(CLK), .clr(Reset));
  Register #(.width(32)) register_17 (.D(_16), .en(and_17_out), .Q(register_17_q), .clk(CLK), .clr(Reset));
  Register #(.width(32)) register_18 (.D(_17), .en(and_18_out), .Q(register_18_q), .clk(CLK), .clr(Reset));
  Register #(.width(32)) register_19 (.D(_18), .en(and_19_out), .Q(register_19_q), .clk(CLK), .clr(Reset));
  Register #(.width(32)) register_20 (.D(_19), .en(and_20_out), .Q(register_20_q), .clk(CLK), .clr(Reset));
  Register #(.width(32)) register_21 (.D(_20), .en(and_21_out), .Q(register_21_q), .clk(CLK), .clr(Reset));
  Register #(.width(32)) register_22 (.D(_21), .en(and_22_out), .Q(register_22_q), .clk(CLK), .clr(Reset));
  Register #(.width(32)) register_23 (.D(_22), .en(and_23_out), .Q(register_23_q), .clk(CLK), .clr(Reset));
  Register #(.width(32)) register_24 (.D(_23), .en(and_24_out), .Q(register_24_q), .clk(CLK), .clr(Reset));
  Register #(.width(32)) register_25 (.D(_24), .en(and_25_out), .Q(register_25_q), .clk(CLK), .clr(Reset));
  Register #(.width(32)) register_26 (.D(_25), .en(and_26_out), .Q(register_26_q), .clk(CLK), .clr(Reset));
  Register #(.width(32)) register_27 (.D(_26), .en(and_27_out), .Q(register_27_q), .clk(CLK), .clr(Reset));
  Register #(.width(32)) register_28 (.D(_27), .en(and_28_out), .Q(register_28_q), .clk(CLK), .clr(Reset));
  Register #(.width(32)) register_29 (.D(_28), .en(and_29_out), .Q(register_29_q), .clk(CLK), .clr(Reset));
  Register #(.width(32)) register_30 (.D(_29), .en(and_30_out), .Q(register_30_q), .clk(CLK), .clr(Reset));
  Register #(.width(32)) register_31 (.D(_30), .en(and_31_out), .Q(register_31_q), .clk(CLK), .clr(Reset));
  Register #(.width(32)) register_32 (.D(_31), .en(and_32_out), .Q(register_32_q), .clk(CLK), .clr(Reset));
  Multiplexer #(.select(5), .width(32)) multiplexer_1 (
    .in0(register_1_q), .in1(register_2_q), .in2(register_3_q), .in3(register_4_q), .in4(register_5_q),
    .in5(register_6_q), .in6(register_7_q), .in7(register_8_q), .in8(register_9_q), .in9(register_10_q),
    .in10(register_11_q), .in11(register_12_q), .in12(register_13_q), .in13(register_14_q),
    .in14(register_15_q), .in15(register_16_q), .in16(register_17_q), .in17(register_18_q),
    .in18(register_19_q), .in19(register_20_q), .in20(register_21_q), .in21(register_22_q),
    .in22(register_23_q), .in23(register_24_q), .in24(register_25_q), .in25(register_26_q),
    .in26(register_27_q), .in27(register_28_q), .in28(register_29_q), .in29(register_30_q),
    .in30(register_31_q), .in31(register_32_q), .out(RD1), .sel(A1));  // open: en
  Multiplexer #(.select(5), .width(32)) multiplexer_2 (
    .in0(register_1_q), .in1(register_2_q), .in2(register_3_q), .in3(register_4_q), .in4(register_5_q),
    .in5(register_6_q), .in6(register_7_q), .in7(register_8_q), .in8(register_9_q), .in9(register_10_q),
    .in10(register_11_q), .in11(register_12_q), .in12(register_13_q), .in13(register_14_q),
    .in14(register_15_q), .in15(register_16_q), .in16(register_17_q), .in17(register_18_q),
    .in18(register_19_q), .in19(register_20_q), .in20(register_21_q), .in21(register_22_q),
    .in22(register_23_q), .in23(register_24_q), .in24(register_25_q), .in25(register_26_q),
    .in26(register_27_q), .in27(register_28_q), .in28(register_29_q), .in29(register_30_q),
    .in30(register_31_q), .in31(register_32_q), .out(RD2), .sel(A2));  // open: en

  // Notes on the sheet:
  //   10
  //   15
endmodule

module PC (
  input  [31:0] NPC,
  input  reset,
  input  clk,
  output [31:0] PC
);

  wire [31:0] register_1_q, xor_1_out;

  assign xor_1_out = 32'h3000 ^ NPC;  // XOR_Gate xor_1, 32 bits wide
  Register #(.width(32)) register_1 (.D(xor_1_out), .Q(register_1_q), .clk(clk), .clr(reset));  // open: en
  assign PC = 32'h3000 ^ register_1_q;  // XOR_Gate xor_2, 32 bits wide
endmodule

module IM (
  input  [31:0] PC,
  output [31:0] opcode
);

  wire [23:0] bit_extender_1_out;
  wire [31:0] shifter_1_out, subtractor_1_out;

  Subtractor #(.width(32)) subtractor_1 (.a(PC), .b(32'h3000), .out(subtractor_1_out));  // open: bin, bout
  Shifter #(.width(32), .shift("lr")) shifter_1 (.in(subtractor_1_out), .\dist (5'b00010), .out(shifter_1_out));
  Bit_Extender #(.in_width(32), .out_width(24)) bit_extender_1 (.in(shifter_1_out), .out(bit_extender_1_out));
  ROM #(.addrWidth(24), .dataWidth(32)) rom_1 (.addr(bit_extender_1_out), .data(opcode));  // open: sel

  // Notes on the sheet:
  //   34210001
  //   34420002
  //   34630003
  //   34210001
  //   1
  //   1
  //   2
  //   2
  //   3
  //   3
  //   1
  //   4
  //   contents of rom_1 (hex, n*v repeats v):
  //   34210001 34420002 34630003 34210001
endmodule

module Controler (
  input  [5:0] in_1,
  input  [5:0] in_2,
  output [2:0] NPCslt,
  output grfWE,
  output EXTOp,
  output [3:0] \type ,
  output ALUsrc,
  output [1:0] RegDst,
  output [1:0] MomtoReg,
  output DMWE
);

  wire add, and_3_out, and_4_out, and_5_out, and_6_out, and_7_out, and_8_out, and_9_out, beq,
       comparator_1_eq, comparator_11_eq, comparator_12_eq, comparator_13_eq, comparator_14_eq,
       comparator_15_eq, comparator_16_eq, comparator_17_eq, comparator_18_eq, comparator_19_eq,
       comparator_20_eq, j, jal, lb, lui, lw, \new , ori, priority_encoder_1_gs, sub, sw;
  wire [3:0] priority_encoder_1_out;

  Priority_Encoder #(.select(4)) priority_encoder_1 (
    .in1(add), .in2(sub), .in3(ori), .in4(lw), .in5(sw), .in6(beq), .in7(lui), .in8(j), .in9(jal), .in10(lb),
    .in11(\new ), .out(priority_encoder_1_out), .gs(priority_encoder_1_gs));  // open: in0, in12, in13, in14, in15, en_out, en_in
  Multiplexer #(.width(4)) multiplexer_1 (
    .in0(4'b0000), .in1(priority_encoder_1_out), .out(\type ), .sel(priority_encoder_1_gs));  // open: en
  Comparator #(.width(6), .mode("unsigned")) comparator_1 (
    .a(in_1), .b({6{1'b0}}), .eq(comparator_1_eq));  // open: gt, lt
  Comparator #(.width(6), .mode("unsigned")) comparator_2 (.a(in_1), .b(6'b001101), .eq(ori));  // open: gt, lt
  Comparator #(.width(6), .mode("unsigned")) comparator_3 (.a(in_1), .b(6'b100011), .eq(lw));  // open: gt, lt
  Comparator #(.width(6), .mode("unsigned")) comparator_4 (.a(in_1), .b(6'b101011), .eq(sw));  // open: gt, lt
  Comparator #(.width(6), .mode("unsigned")) comparator_5 (.a(in_1), .b(6'b000100), .eq(beq));  // open: gt, lt
  Comparator #(.width(6), .mode("unsigned")) comparator_6 (.a(in_1), .b(6'b001111), .eq(lui));  // open: gt, lt
  Comparator #(.width(6), .mode("unsigned")) comparator_7 (.a(in_1), .b(6'b000010), .eq(j));  // open: gt, lt
  Comparator #(.width(6), .mode("unsigned")) comparator_8 (.a(in_1), .b(6'b000011), .eq(jal));  // open: gt, lt
  Comparator #(.width(6), .mode("unsigned")) comparator_9 (.a(in_1), .b(6'b100000), .eq(lb));  // open: gt, lt
  Comparator #(.width(6), .mode("unsigned")) comparator_10 (.a(in_1), .b(6'b011000), .eq(\new ));  // open: gt, lt
  Comparator #(.width(6), .mode("unsigned")) comparator_11 (
    .a(in_1), .b({6{1'b0}}), .eq(comparator_11_eq));  // open: gt, lt
  Multiplexer #(.select(4)) multiplexer_2 (
    .in0(1'b0), .in1(1'b0), .in2(1'b0), .in3(1'b1), .in4(1'b1), .in5(1'b1), .in6(1'b0), .in7(1'b1),
    .in8(1'b0), .in9(1'b0), .in10(1'b1), .in11(1'b1), .out(ALUsrc), .sel(\type ));  // open: in12, in13, in14, in15, en
  Comparator #(.width(6), .mode("unsigned")) comparator_12 (
    .a(in_2), .b(6'b100000), .eq(comparator_12_eq));  // open: gt, lt
  Comparator #(.width(6), .mode("unsigned")) comparator_13 (
    .a(in_2), .b(6'b100010), .eq(comparator_13_eq));  // open: gt, lt
  Comparator #(.width(6), .mode("unsigned")) comparator_14 (
    .a(in_2), .b({6{1'b0}}), .eq(comparator_14_eq));  // open: gt, lt
  Comparator #(.width(6), .mode("unsigned")) comparator_15 (
    .a(in_2), .b({6{1'b0}}), .eq(comparator_15_eq));  // open: gt, lt
  Comparator #(.width(6), .mode("unsigned")) comparator_16 (
    .a(in_2), .b({6{1'b0}}), .eq(comparator_16_eq));  // open: gt, lt
  Comparator #(.width(6), .mode("unsigned")) comparator_17 (
    .a(in_2), .b({6{1'b0}}), .eq(comparator_17_eq));  // open: gt, lt
  Comparator #(.width(6), .mode("unsigned")) comparator_18 (
    .a(in_2), .b({6{1'b0}}), .eq(comparator_18_eq));  // open: gt, lt
  Comparator #(.width(6), .mode("unsigned")) comparator_19 (
    .a(in_2), .b({6{1'b0}}), .eq(comparator_19_eq));  // open: gt, lt
  Comparator #(.width(6), .mode("unsigned")) comparator_20 (
    .a(in_2), .b({6{1'b0}}), .eq(comparator_20_eq));  // open: gt, lt
  Multiplexer #(.select(4), .width(3)) multiplexer_3 (
    .in0(3'b000), .in1(3'b000), .in2(3'b000), .in3(3'b000), .in4(3'b000), .in5(3'b000), .in6(3'b001),
    .in7(3'b000), .in8(3'b010), .in9(3'b010), .in10(3'b000), .in11(3'b000), .out(NPCslt), .sel(\type ));  // open: in12, in13, in14, in15, en
  and and_1 (add, comparator_1_eq, comparator_12_eq);
  and and_2 (sub, comparator_1_eq, comparator_13_eq);
  and and_3 (and_3_out, comparator_1_eq, comparator_14_eq);
  and and_4 (and_4_out, comparator_1_eq, comparator_15_eq);
  and and_5 (and_5_out, comparator_1_eq, comparator_16_eq);
  and and_6 (and_6_out, comparator_1_eq, comparator_17_eq);
  and and_7 (and_7_out, comparator_1_eq, comparator_18_eq);
  and and_8 (and_8_out, comparator_1_eq, comparator_19_eq);
  and and_9 (and_9_out, comparator_1_eq, comparator_20_eq);
  Multiplexer #(.select(4)) multiplexer_4 (
    .in0(1'b0), .in1(1'b1), .in2(1'b1), .in3(1'b1), .in4(1'b1), .in5(1'b0), .in6(1'b0), .in7(1'b1),
    .in8(1'b0), .in9(1'b1), .in10(1'b1), .in11(1'b0), .out(grfWE), .sel(\type ));  // open: in12, in13, in14, in15, en
  Multiplexer #(.select(4), .width(2)) multiplexer_5 (
    .in0(2'b00), .in1(2'b01), .in2(2'b01), .in3(2'b00), .in4(2'b00), .in5(2'b00), .in6(2'b00), .in7(2'b00),
    .in8(2'b00), .in9(2'b10), .in10(2'b00), .in11(2'b11), .out(RegDst), .sel(\type ));  // open: in12, in13, in14, in15, en
  Multiplexer #(.select(4)) multiplexer_6 (
    .in0(1'b0), .in1(1'b0), .in2(1'b0), .in3(1'b0), .in4(1'b1), .in5(1'b1), .in6(1'b0), .in7(1'b0),
    .in8(1'b0), .in9(1'b0), .in10(1'b1), .in11(1'b1), .out(EXTOp), .sel(\type ));  // open: in12, in13, in14, in15, en
  Multiplexer #(.select(4), .width(2)) multiplexer_7 (
    .in0(2'b00), .in1(2'b00), .in2(2'b00), .in3(2'b00), .in4(2'b01), .in5(2'b00), .in6(2'b00), .in7(2'b00),
    .in8(2'b00), .in9(2'b10), .in10(2'b11), .in11(2'b10), .out(MomtoReg), .sel(\type ));  // open: in12, in13, in14, in15, en
  Multiplexer #(.select(4)) multiplexer_8 (
    .in0(1'b0), .in1(1'b0), .in2(1'b0), .in3(1'b0), .in4(1'b0), .in5(1'b1), .in6(1'b0), .in7(1'b0),
    .in8(1'b0), .in9(1'b0), .in10(1'b0), .in11(1'b0), .out(DMWE), .sel(\type ));  // open: in12, in13, in14, in15, en

  // Other names for the same wires on the sheet: func[5:0] = in_2; Opcode[5:0] = in_1
endmodule

module ALU (
  input  [3:0] \type ,
  input  [31:0] inA,
  input  [31:0] inB,
  output [31:0] out_4,
  output zero
);

  wire zero_t;
  wire [31:0] tunnel, tunnel_t, tunnel_t_t, undriven;

  Multiplexer #(.select(4)) multiplexer_1 (
    .in6(zero_t), .out(zero), .sel(\type ));  // open: in0, in1, in2, in3, in4, in5, in7, in8, in9, in10, in11, in12, in13, in14, in15, en
  Adder #(.width(32)) adder_1 (.a(inA), .b(inB), .out(tunnel));  // open: cin, cout
  Multiplexer #(.select(4), .width(32)) multiplexer_2 (
    .in1(tunnel), .in2(tunnel_t), .in3(tunnel_t_t), .in4(tunnel), .in5(tunnel),
    .in7({inB[15:0], {16{1'b0}}}), .in10(tunnel), .in11(undriven), .out(out_4), .sel(\type ));  // open: in0, in6, in8, in9, in12, in13, in14, in15, en
  Subtractor #(.width(32)) subtractor_1 (.a(inA), .b(inB), .out(tunnel_t));  // open: bin, bout
  assign tunnel_t_t = inA | inB;  // OR_Gate or_1, 32 bits wide
  Comparator #(.width(32), .mode("unsigned")) comparator_1 (.a(inA), .b(inB), .eq(zero_t));  // open: gt, lt

  // Other names for the same wires on the sheet: lui[31:16] = inB[15:0]

  // Notes on the sheet:
  //          1011is new
endmodule

module EXT (
  input  [15:0] in_1,
  input  EXTOp,
  output [31:0] out_3
);

  wire [31:0] bit_extender_1_out, bit_extender_2_out;

  assign bit_extender_1_out = {{16{1'b0}}, in_1};  // Bit_Extender bit_extender_1
  assign bit_extender_2_out = {{16{in_1[15]}}, in_1};  // Bit_Extender bit_extender_2
  Multiplexer #(.width(32)) multiplexer_1 (
    .in0(bit_extender_1_out), .in1(bit_extender_2_out), .out(out_3), .sel(EXTOp));  // open: en
endmodule

module DM (
  input  [31:0] Addr,
  input  WE,
  input  clk,
  input  Re,
  input  [31:0] WD,
  output [31:0] Data,
  output [31:0] \byte 
);

  wire [7:0] bitselector_1_out;
  wire [23:0] bit_extender_1_out;
  wire [31:0] shifter_1_out;

  Shifter #(.width(32), .shift("lr")) shifter_1 (.in(Addr), .\dist (5'b00010), .out(shifter_1_out));
  Bit_Extender #(.in_width(32), .out_width(24)) bit_extender_1 (.in(shifter_1_out), .out(bit_extender_1_out));
  RAM #(.addrWidth(24), .dataWidth(32), .bus("separate")) ram_1 (
    .addr(bit_extender_1_out), .din(WD), .data(Data), .str(WE), .clk(clk), .clr(Re));  // open: sel, ld
  BitSelector #(.width(32), .group(8)) bitselector_1 (.in(Data), .out(bitselector_1_out), .sel(Addr[1:0]));
  assign \byte  = {{24{1'b0}}, bitselector_1_out};  // Bit_Extender bit_extender_2

  // Other names for the same wires on the sheet: Addr_1_0[1:0] = Addr[1:0]
endmodule
